# Fritzing sketch OTP (saved by Fritzing 0.9.10b)
breadboards: 1

parts:
  U2 = LuaNode32 / ESP32 [part_number=ESP32S-PIN30]
  J1 = Piezo Speaker
  OLED1 = OLED 128x64 I2C Monochrome Display
  VCC1 = 4 x AAA Battery Mount
  U3 = SWITCH-SPST-2 [package=switch-spst-vertical]

nets:
  GND: U2.GND, J1.pin1, OLED1.GND, VCC1.-
  N1: U2.Vin, U3.O
  3V3: U2.3V3, OLED1.VDD
  N2: U2.D4, J1.pin2
  N3: U2.D21, OLED1.SCK
  N4: U2.D22, OLED1.SDA
  N5: VCC1.+, U3.P

custom parts:
  LuaNode32 / ESP32: New Image for LuaNode32 DOIT ESP32 DEVKIT V1. Base parts from LuaNode32 / ESP32 ESP32 based LuaNode32 by G.Noorlander DOIT Esp32 DevKit v1 (30 pins long, 11 pins width) by Werner Rothschopf (modified by vanepp Dec 2018)
